# Fritzing sketch nixie_i2c_driver_stackable (saved by Fritzing 0.9.3b)
circuit board: 5.09512cm x 6.0163cm

parts:
  I2C_-_PCF8574 = PCF8574 [package="DIP16 [THT]"]
  HV_PWR = IC, SIP package, 5 pins [chip_label=IC]
  74141 = IC, DIP package, 16 pins [chip_label=74141]
  STACK_PWR = SIP - 2 pins [chip_label=PWR package="SIP (Single Inline) [THT]"]
  I2C = SIP - 2 pins [chip_label=Bus package="SIP (Single Inline) [THT]"]
  SW1 = DIP SWITCH [package=dipswitch-02]
  SW2 = DIP SWITCH [package=dipswitch-02]
  R2 = Resistor [tolerance=±5% resistance=10k package=THT]
  C1 = Tantalum Capacitor [capacitance=0.1µF package="100 mil [THT, tantalum]"]
  C2 = Tantalum Capacitor [capacitance=0.1µF package="100 mil [THT, tantalum]"]
  C3 = Tantalum Capacitor [capacitance=0.1µF package="100 mil [THT, tantalum]"]
  R1 = Resistor [tolerance=±5% resistance=10k package=THT]
  R3 = Resistor [tolerance=±5% resistance=10k package=THT]
  R4 = Resistor [tolerance=±5% resistance=10k package=THT]
  R5 = Resistor [tolerance=±5% resistance=10k package=THT]
  Anode = double row male pin header, 6 pins [form="♂ (male)"]
  R6 = Resistor [tolerance=±5% resistance=10 power=2W package=THT]
  R7 = Resistor [tolerance=±5% resistance=10 power=2W package=THT]
  R8 = Resistor [tolerance=±5% resistance=10k package=THT]
  PWR = Header 2 [package=screwterminal-3.5mm-2_lock]
  74141_2 = IC, DIP package, 16 pins [chip_label=74141]
  NX_1 = double row male pin header, 10 pins [form="♂ (male)"]
  NX_2 = double row male pin header, 10 pins [form="♂ (male)"]

nets:
  N1: I2C_-_PCF8574.A0, SW1.1, R5.Pin_0
  N2: I2C_-_PCF8574.A1, SW2.2, R4.Pin_0
  N3: I2C_-_PCF8574.A3, SW2.1, R3.Pin_0
  A0: I2C_-_PCF8574.P0, 74141.pin3
  B0: I2C_-_PCF8574.P1, 74141.pin6
  C0: I2C_-_PCF8574.P2, 74141.pin7
  D0: I2C_-_PCF8574.P3, 74141.pin4
  GND: I2C_-_PCF8574.GND, HV_PWR.pin2, HV_PWR.pin4, 74141.pin12, STACK_PWR.pin2, C1.-, C2.-, C3.-, R3.Pin_1, R4.Pin_1, R5.Pin_1, R8.Pin_1, PWR.2, 74141_2.pin12
  A1: I2C_-_PCF8574.P4, 74141_2.pin3
  B1: I2C_-_PCF8574.P5, 74141_2.pin6
  C1: I2C_-_PCF8574.P6, 74141_2.pin7
  D1: I2C_-_PCF8574.P7, 74141_2.pin4
  N4: I2C_-_PCF8574.SCL, I2C.pin2, R2.Pin_1
  N5: I2C_-_PCF8574.SDA, I2C.pin1, R1.Pin_1
  5V: I2C_-_PCF8574.VCC, HV_PWR.pin1, 74141.pin5, STACK_PWR.pin1, SW1.3, SW1.4, SW2.3, SW2.4, R2.Pin_0, C1.+, C2.+, C3.+, R1.Pin_0, PWR.1, 74141_2.pin5
  HV EN: HV_PWR.pin3, SW1.2, R8.Pin_0
  170V: HV_PWR.pin5, R6.Pin_0, R7.Pin_0
  N6: 74141.pin1, NX_1.pin9
  N7: 74141.pin2, NX_1.pin10
  N8: 74141.pin8, NX_1.pin3
  N9: 74141.pin9, NX_1.pin4
  N10: 74141.pin10, NX_1.pin8
  N11: 74141.pin11, NX_1.pin7
  N12: 74141.pin13, NX_1.pin5
  N13: 74141.pin14, NX_1.pin6
  N14: 74141.pin15, NX_1.pin2
  N15: 74141.pin16, NX_1.pin1
  N16: Anode.pin1, Anode.pin2, Anode.pin3, R6.Pin_1
  N17: Anode.pin4, Anode.pin5, Anode.pin6, R7.Pin_1
  N18: 74141_2.pin1, NX_2.pin9
  N19: 74141_2.pin2, NX_2.pin10
  N20: 74141_2.pin8, NX_2.pin3
  N21: 74141_2.pin9, NX_2.pin4
  N22: 74141_2.pin10, NX_2.pin8
  N23: 74141_2.pin11, NX_2.pin7
  N24: 74141_2.pin13, NX_2.pin5
  N25: 74141_2.pin14, NX_2.pin6
  N26: 74141_2.pin15, NX_2.pin2
  N27: 74141_2.pin16, NX_2.pin1

notes:
  Nixie i2c Driver, This chip is indended to be used with angled pin headers for the nixie tubes in order to stack the modules on top of each other, 1
  5v gnd en gnd hv
  5v gnd
  SCL SDA
  A2 A1 A0 EN
  4 3 2 1 0
  5 6 7 8 9
  Nixie i2c Driver
  rev 1 - 25.11.2017
  IN-4 tubes have 3<module fritzingVersion="0.9.3b.04.19.5c895d327c44a3114e5fcc9d8260daf0cbb52806">
  <boundingRects>
  <boundingRect rect="275 199.15 216 11.7" name="Schaltplanansicht"/>
  <boundingRect rect="0 0 0 0" name="Steckplatinenansicht"/>
  <boundingRect rect="0 0 0 0" name="Leiterplattenansicht"/>
  </boundingRects>
  <instances>
  <instance modelIndex="85467566" moduleIdRef="SchematicLogoTextModuleID" path=":/resources/parts/core/schematiclogotext.fzp">
  <property value="IN-4 tubes have 3 anodes" name="logo"/>
  <property value="60.960000000000008" name="width"/>
  <property value="3.302" name="height"/>
  <property value="&lt;svg width=&quot;2.4in&quot; viewBox=&quot;0 0 240 13&quot; xmlns=&quot;http://www.w3.org/2000/svg&quot; height=&quot;.13in&quot;>&#xa; &lt;g id=&quot;schematic&quot;>&#xa; &lt;text fill=&quot;black&quot; font-family=&quot;Droid Sans&quot; font-size=&quot;10&quot; id=&quot;label&quot; stroke-width=&quot;0&quot; xml:space=&quot;preserve&quot; x=&quot;120&quot; y=&quot;9&quot; text-anchor=&quot;middle&quot;>IN-4 tubes have 3 anodes&lt;/text>&#xa; &lt;/g>&#xa;&lt;/svg>&#xa;" name="shape"/>
  <property value=":/resources/parts/svg/core/schematic/schematiclogo.svg" name="lastfilename"/>
  <title>TXT3</title>
  <views>
  <schematicView layer="schematicText">
  <geometry x="275" y="199.15" z="4.00215"/>
  </schematicView>
  <breadboardView layer="">
  <geometry x="284.839" y="126.629" z="0"/>
  </breadboardView>
  <pcbView layer="">
  <geometry x="918.25" y="379.4" z="0"/>
  </pcbView>
  </views>
  </instance>
  </instances>
  </module>
  anodes
  but the driver supports all kinds of nixie tubes
  Supply HV power here. Matching small HV modules can be stacked on top.
  When stacking, the topmost driver can supply power to all modules below
  The i2c driver is dynamically adressable using the three dip switches
  The fourth switch is used to enable / disable the HV module. Note: some hv modules have an inverten EN input!
  Pin 1 -> 0
  Pin 10 -> 9
