# Fritzing sketch nixie_i2c_driver_stackable_v2 (saved by Fritzing 0.9.3b)
circuit board: 4.90697cm x 6.0163cm

parts:
  I2C_-_PCF8574 = PCF8574 [package="DIP16 [THT]"]
  I2C = SIP - 2 pins [chip_label=Bus package="SIP (Single Inline) [THT]"]
  C1 = Tantalum Capacitor [capacitance=0.1µF package="100 mil [THT, tantalum]"]
  C2 = Tantalum Capacitor [capacitance=0.1µF package="100 mil [THT, tantalum]"]
  C3 = Tantalum Capacitor [capacitance=0.1µF package="100 mil [THT, tantalum]"]
  Anode = double row male pin header, 6 pins [form="♂ (male)"]
  R6 = Resistor [tolerance=±5% resistance=10 power=2W package=THT]
  R7 = Resistor [tolerance=±5% resistance=10 power=2W package=THT]
  74141 = IC, DIP package, 16 pins [chip_label=74141]
  NX_1 = double row male pin header, 10 pins [form="♂ (male)"]
  NX_2 = double row male pin header, 10 pins [form="♂ (male)"]
  74141_2 = IC, DIP package, 16 pins [chip_label=74141]
  J1 = male pin header, 3 pins [form="♂ (male)"]
  J2 = male pin header, 3 pins [form="♂ (male)"]
  IC_PWR = SIP - 2 pins [chip_label=PWR package="SIP (Single Inline) [THT]"]
  I2C1 = SIP - 2 pins [chip_label=Bus package="SIP (Single Inline) [THT]"]
  IC_PWR_2 = SIP - 2 pins [chip_label=PWR package="SIP (Single Inline) [THT]"]
  IC_PWR2 = SIP - 2 pins [chip_label=PWR package="SIP (Single Inline) [THT]"]
  J3 = male pin header, 3 pins [form="♂ (male)"]
  HV_PWR = IC, SIP package, 3 pins [chip_label=IC]
  HV_PWR_2 = IC, SIP package, 3 pins [chip_label=IC]
  D2 = Diode [package=diode-1n4001]
  J4 = male pin header, 2 pins [form="♂ (male)"]
  R2 = Resistor [tolerance=±5% resistance=1k power=0.5W package=THT]
  R1 = Resistor [tolerance=±5% resistance=1k power=0.5W package=THT]

nets:
  N1: I2C_-_PCF8574.A0, J1.pin2
  N2: I2C_-_PCF8574.A1, J2.pin2
  N3: I2C_-_PCF8574.A3, J3.pin2
  A0: I2C_-_PCF8574.P0, 74141_2.pin3
  B0: I2C_-_PCF8574.P1, 74141_2.pin6
  C0: I2C_-_PCF8574.P2, 74141_2.pin7
  D0: I2C_-_PCF8574.P3, 74141_2.pin4
  GND: I2C_-_PCF8574.GND, C1.-, C2.-, C3.-, 74141.pin12, 74141_2.pin12, J1.pin3, J2.pin3, IC_PWR.pin2, IC_PWR_2.pin2, IC_PWR2.pin2, J3.pin3, D2.A, J4.pin1
  A1: I2C_-_PCF8574.P4, 74141.pin3
  B1: I2C_-_PCF8574.P5, 74141.pin6
  C1: I2C_-_PCF8574.P6, 74141.pin7
  D1: I2C_-_PCF8574.P7, 74141.pin4
  N4: I2C_-_PCF8574.SCL, I2C.pin2, I2C1.pin2, R2.Pin_1
  N5: I2C_-_PCF8574.SDA, I2C.pin1, I2C1.pin1, R1.Pin_1
  5V: I2C_-_PCF8574.VCC, C1.+, C2.+, C3.+, 74141.pin5, 74141_2.pin5, J1.pin1, J2.pin1, IC_PWR.pin1, IC_PWR_2.pin1, IC_PWR2.pin1, J3.pin1, D2.C, R2.Pin_0, R1.Pin_0
  N6: Anode.pin1, Anode.pin2, Anode.pin3, R6.Pin_1
  N7: Anode.pin4, Anode.pin5, Anode.pin6, R7.Pin_1
  170V: R6.Pin_0, R7.Pin_0, HV_PWR.pin3, HV_PWR_2.pin3
  N8: 74141.pin1, NX_2.pin9
  N9: 74141.pin2, NX_2.pin10
  N10: 74141.pin8, NX_2.pin3
  N11: 74141.pin9, NX_2.pin4
  N12: 74141.pin10, NX_2.pin8
  N13: 74141.pin11, NX_2.pin7
  N14: 74141.pin13, NX_2.pin5
  N15: 74141.pin14, NX_2.pin6
  N16: 74141.pin15, NX_2.pin2
  N17: 74141.pin16, NX_2.pin1
  N18: NX_1.pin1, 74141_2.pin16
  N19: NX_1.pin2, 74141_2.pin15
  N20: NX_1.pin3, 74141_2.pin8
  N21: NX_1.pin4, 74141_2.pin9
  N22: NX_1.pin5, 74141_2.pin13
  N23: NX_1.pin6, 74141_2.pin14
  N24: NX_1.pin7, 74141_2.pin11
  N25: NX_1.pin8, 74141_2.pin10
  N26: NX_1.pin9, 74141_2.pin1
  N27: NX_1.pin10, 74141_2.pin2
  N28: HV_PWR.pin1, HV_PWR.pin2, HV_PWR_2.pin1, HV_PWR_2.pin2, J4.pin2

notes:
  Nixie i2c Driver, This chip is indended to be used with angled pin headers for the nixie tubes in order to stack the modules on top of each other, 1
  GND  HV
  5v gnd
  SCL SDA
  A2
  4 3 2 1 0
  5 6 7 8 9
  NI2C - Nixie i2c Driver
  rev 2 - 10.12.2017
  Supply HV power here. Matching small HV modules can be stacked on top.
  When stacking, the topmost driver can supply power to all modules below
  The i2c driver is dynamically adressable using the three dip switches
  The fourth switch is used to enable / disable the HV module. Note: some hv modules have an inverten EN input!
  Pin 1 -> 0
  Pin 10 -> 9
  IN-4 tubes have 3 anodes but the driver supports all kinds of nixie tubes
  A0
  GND
  5V
  A1
  GND BRIDGE
  5
  1
  git.io/vbuzM
  code
  -n-
  fold
