# Fritzing sketch nixie_shift_register_driver (saved by Fritzing 0.9.3b)
circuit board: 7.18457cm x 7.5639cm
breadboards: 1

parts:
  NX1 = SN74141 [package="DIP16 [THT]"]
  NX2 = SN74141 [package="DIP16 [THT]"]
  SHIFT = 74HC595 [package="DIP16 [THT]"]
  IN = female pin header, 6 pins [form="♀ (female)"]
  OUT = female pin header, 6 pins [form="♀ (female)"]
  ANODE = female pin header, 6 pins [form="♀ (female)"]
  4k7_2W = Resistor [tolerance=±5% resistance=4.7k package=THT]
  4k7_2W_2 = Resistor [tolerance=±5% resistance=4.7k package=THT]
  GND = female pin header, 2 pins [form="♀ (female)"]
  HV = female pin header, 2 pins [form="♀ (female)"]
  HV_2 = female pin header, 2 pins [form="♀ (female)"]
  GND_2 = female pin header, 2 pins [form="♀ (female)"]
  NIXIE_2 = double row male pin header, 10 pins [form="♂ (male)"]
  NIXIE_1 = double row male pin header, 10 pins [form="♂ (male)"]
  J2 = Screw terminal - 2 pins [package=THT]
  J1 = Screw terminal - 2 pins [package=THT]

nets:
  N1: NX1.8, NIXIE_1.pin9
  N2: NX1.9, NIXIE_1.pin10
  N3: NX1.A, SHIFT.Q0
  N4: NX1.D, SHIFT.Q3
  5V: NX1.VCC, NX2.VCC, SHIFT.MR, SHIFT.VCC, IN.pin5, OUT.pin5
  N5: NX1.B, SHIFT.Q1
  N6: NX1.C, SHIFT.Q2
  N7: NX1.2, NIXIE_1.pin3
  N8: NX1.3, NIXIE_1.pin4
  N9: NX1.7, NIXIE_1.pin8
  N10: NX1.6, NIXIE_1.pin7
  GND: NX1.GND, NX2.GND, SHIFT.GND, SHIFT.OE, IN.pin6, OUT.pin6, GND.pin1, GND.pin2, GND_2.pin1, GND_2.pin2, J2.pin1, J1.pin2
  N11: NX1.4, NIXIE_1.pin5
  N12: NX1.5, NIXIE_1.pin6
  N13: NX1.1, NIXIE_1.pin2
  N14: NX1.0, NIXIE_1.pin1
  N15: NX2.8, NIXIE_2.pin9
  N16: NX2.9, NIXIE_2.pin10
  N17: NX2.A, SHIFT.Q4
  N18: NX2.D, SHIFT.Q7
  N19: NX2.B, SHIFT.Q5
  N20: NX2.C, SHIFT.Q6
  N21: NX2.2, NIXIE_2.pin3
  N22: NX2.3, NIXIE_2.pin4
  N23: NX2.7, NIXIE_2.pin8
  N24: NX2.6, NIXIE_2.pin7
  N25: NX2.4, NIXIE_2.pin5
  N26: NX2.5, NIXIE_2.pin6
  N27: NX2.1, NIXIE_2.pin2
  N28: NX2.0, NIXIE_2.pin1
  N29: SHIFT.Q7', OUT.pin2
  N30: SHIFT.SH_CP, IN.pin4, OUT.pin4
  N31: SHIFT.ST_CP, IN.pin3, OUT.pin3
  N32: SHIFT.DS, IN.pin2
  N33: ANODE.pin1, ANODE.pin2, ANODE.pin3, 4k7_2W.Pin_1
  N34: ANODE.pin4, ANODE.pin5, ANODE.pin6, 4k7_2W_2.Pin_1
  N35: 4k7_2W.Pin_0, 4k7_2W_2.Pin_0, HV.pin1, HV.pin2, HV_2.pin1, HV_2.pin2, J2.pin2, J1.pin1

notes:
  HV
  GND
  ANODE
  NIXIE TUBE 1
  NIXIE TUBE 2
  ST_CP
  Q7*
  SH_CP
  5V
  0
  1
  2
  3
  4
  5
  7
  8
  9
  6
  Nixie Universal Serial Driver V0.1

custom parts:
  SN74141: The SN74141 is a secondegeneration BCD to decima decoder designed specifically to drive cold cathode tubes
